// Logisim project Q1_logic4.circ as structural Verilog
module main (
  input  a,
  input  b,
  input  c,
  input  d,
  output out1,
  output out2
);

  logic4 logic4_1 (.a(a), .b(b), .c(c), .d(d), .out1(out1), .out2(out2));
endmodule

// VHDL entity logic4, as the project stores it:
library ieee;
use ieee.std_logic_1164.all;

entity logic4 is
    port (
        a, b, c, d : in std_logic;
        out1, out2 : out std_logic
    );
end entity logic4;

architecture bhv of logic4 is
begin
    out1 <= a and b and c and d;
    out2 <= a or b or c or d;
end architecture bhv;
