// Logisim project Q2_mux8.circ as structural Verilog
module main (
  input  a,
  input  b,
  input  c,
  input  d,
  input  e,
  input  f,
  input  g,
  input  h,
  input  [2:0] in_9,
  output out_10
);

  mux8 mux8_1 (.a(a), .b(b), .c(c), .d(d), .e(e), .f(f), .g(g), .h(h), .sel(in_9), .data(out_10));
endmodule

// VHDL entity mux8, as the project stores it:
library ieee;
use ieee.std_logic_1164.all;

entity mux8 is
    port (
        a, b, c, d, e, f, g, h : in std_logic;
        sel : in std_logic_vector(2 downto 0);
        data : out std_logic
    );
end entity mux8;

architecture bhv of mux8 is
begin
    process(a, b, c, d, e, f, g, h, sel)
    begin
        case sel is
            when "000" => data <= a;
            when "001" => data <= b;
            when "010" => data <= c;
            when "011" => data <= d;
            when "100" => data <= e;
            when "101" => data <= f;
            when "110" => data <= g;
            when "111" => data <= h;
            when others => data <= '0';
        end case;
    end process;
end architecture bhv;
