// Logisim project Q3_letters7seg.circ as structural Verilog
module main (
  input  [2:0] dat
);

  wire [7:0] letters7seg_1_display;

  letters7seg letters7seg_1 (.dat(dat), .display(letters7seg_1_display));
  _7_Segment_Display u_7_segment_display_1 (
    .g(letters7seg_1_display[1]), .f(letters7seg_1_display[2]), .a(letters7seg_1_display[7]),
    .b(letters7seg_1_display[6]), .e(letters7seg_1_display[3]), .d(letters7seg_1_display[4]),
    .c(letters7seg_1_display[5]), .dp(letters7seg_1_display[0]));
endmodule

// VHDL entity letters7seg, as the project stores it:
library ieee;
use ieee.std_logic_1164.all;

entity letters7seg is
    port (
        dat : in std_logic_vector(2 downto 0);
        display : out std_logic_vector(7 downto 0)
    );
end entity letters7seg;

architecture bhv of letters7seg is
begin
    process(dat)
    begin
        case dat is
            when "000" => display <= "11111010"; -- a
            when "001" => display <= "00111110"; -- b
            when "010" => display <= "00011010"; -- c
            when "011" => display <= "01111010"; -- d
            when "100" => display <= "10001110"; -- f
            when "101" => display <= "11110110"; -- g
            when others => display <= "00000000";
        end case;
    end process;
end architecture bhv;
